// Logisim project Project 2 (Multiplexer).circ as structural Verilog: 13 circuits, main circuit dec_7seg_driver
module main (
  input  in_1,
  input  in_2,
  input  _1,
  input  _2,
  input  _3,
  input  in_6,
  input  in_7,
  input  in_8,
  input  in_9,
  input  in_10,
  input  in_11,
  input  in_12,
  input  in_13,
  input  in_14,
  input  in_15,
  input  in_16,
  input  in_17,
  input  in_18,
  input  in_19,
  input  in_20,
  input  in_21,
  input  in_22,
  input  _1_2,
  input  _2_2,
  input  _3_2,
  input  in_26,
  input  in_27,
  input  in_28,
  input  in_29,
  input  in_30,
  input  in_31,
  input  in_32,
  input  in_33,
  input  in_34,
  input  in_35,
  input  in_36,
  input  in_37,
  input  in_38
);

  wire dec_7seg_driver_1_a, dec_7seg_driver_1_b, dec_7seg_driver_1_c, dec_7seg_driver_1_d,
       dec_7seg_driver_1_e, dec_7seg_driver_1_f, dec_7seg_driver_1_g, dec_7seg_driver_2_a,
       dec_7seg_driver_2_b, dec_7seg_driver_2_c, dec_7seg_driver_2_d, dec_7seg_driver_2_e,
       dec_7seg_driver_2_f, dec_7seg_driver_2_g, dec_7seg_driver_3_a, dec_7seg_driver_3_b,
       dec_7seg_driver_3_c, dec_7seg_driver_3_d, dec_7seg_driver_3_e, dec_7seg_driver_3_f,
       dec_7seg_driver_3_g, dec_7seg_driver_4_a, dec_7seg_driver_4_b, dec_7seg_driver_4_c,
       dec_7seg_driver_4_d, dec_7seg_driver_4_e, dec_7seg_driver_4_f, dec_7seg_driver_4_g, dec_adder_1_out_9,
       dec_adder_1_out_10, dec_adder_1_out_11, dec_adder_1_out_12, dec_adder_1_out_13,
       n2_to_4_mux_set_1_out_0, n2_to_4_mux_set_1_out_1, n2_to_4_mux_set_1_out_2, n2_to_4_mux_set_1_out_3,
       n2_to_4_mux_set_2_out_0, n2_to_4_mux_set_2_out_1, n2_to_4_mux_set_2_out_2, n2_to_4_mux_set_2_out_3,
       ones_place_1_out_6, ones_place_1_out_7, ones_place_1_out_8, ones_place_1_out_9, tens_place_true_1_h,
       tens_place_true_1_i;

  _2_to_4_mux_set u_2_to_4_mux_set_1 (
    .a0(_1), .b0(_2), .c0(_3), .d0(in_7), .a1(in_8), .b1(in_9), .c1(in_11), .d1(in_12), .a2(in_13),
    .b2(in_14), .c2(in_15), .d2(in_16), .a3(in_17), .b3(in_18), .c3(in_19), .d3(in_20), .S1(in_1), .S0(in_2),
    .out_0(n2_to_4_mux_set_1_out_0), .out_1(n2_to_4_mux_set_1_out_1), .out_2(n2_to_4_mux_set_1_out_2),
    .out_3(n2_to_4_mux_set_1_out_3));
  _2_to_4_mux_set u_2_to_4_mux_set_2 (
    .a0(_1_2), .b0(_2_2), .c0(_3_2), .d0(in_26), .a1(in_27), .b1(in_28), .c1(in_29), .d1(in_30), .a2(in_31),
    .b2(in_32), .c2(in_33), .d2(in_34), .a3(in_35), .b3(in_36), .c3(in_37), .d3(in_38), .S1(in_21),
    .S0(in_22), .out_0(n2_to_4_mux_set_2_out_0), .out_1(n2_to_4_mux_set_2_out_1),
    .out_2(n2_to_4_mux_set_2_out_2), .out_3(n2_to_4_mux_set_2_out_3));
  tens_place_true tens_place_true_1 (
    .A(dec_adder_1_out_9), .B(dec_adder_1_out_10), .C(dec_adder_1_out_11), .D(dec_adder_1_out_12),
    .E(dec_adder_1_out_13), .H(tens_place_true_1_h), .I(tens_place_true_1_i));
  dec_7seg_driver dec_7seg_driver_1 (
    .W(n2_to_4_mux_set_1_out_3), .X(n2_to_4_mux_set_1_out_2), .Y(n2_to_4_mux_set_1_out_1),
    .Z(n2_to_4_mux_set_1_out_0), .A(dec_7seg_driver_1_a), .B(dec_7seg_driver_1_b), .C(dec_7seg_driver_1_c),
    .D(dec_7seg_driver_1_d), .E(dec_7seg_driver_1_e), .F(dec_7seg_driver_1_f), .G(dec_7seg_driver_1_g));
  dec_7seg_driver dec_7seg_driver_2 (
    .W(n2_to_4_mux_set_2_out_3), .X(n2_to_4_mux_set_2_out_2), .Y(n2_to_4_mux_set_2_out_1),
    .Z(n2_to_4_mux_set_2_out_0), .A(dec_7seg_driver_2_a), .B(dec_7seg_driver_2_b), .C(dec_7seg_driver_2_c),
    .D(dec_7seg_driver_2_d), .E(dec_7seg_driver_2_e), .F(dec_7seg_driver_2_f), .G(dec_7seg_driver_2_g));
  dec_adder dec_adder_1 (
    .in_1(n2_to_4_mux_set_1_out_3), .in_2(n2_to_4_mux_set_1_out_2), .in_3(n2_to_4_mux_set_1_out_1),
    .in_4(n2_to_4_mux_set_1_out_0), .in_5(n2_to_4_mux_set_2_out_3), .in_6(n2_to_4_mux_set_2_out_2),
    .in_7(n2_to_4_mux_set_2_out_1), .in_8(n2_to_4_mux_set_2_out_0), .out_9(dec_adder_1_out_9),
    .out_10(dec_adder_1_out_10), .out_11(dec_adder_1_out_11), .out_12(dec_adder_1_out_12),
    .out_13(dec_adder_1_out_13));
  _7_Segment_Display u_7_segment_display_1 (
    .g(dec_7seg_driver_1_g), .f(dec_7seg_driver_1_f), .a(dec_7seg_driver_1_a), .b(dec_7seg_driver_1_b),
    .e(dec_7seg_driver_1_e), .d(dec_7seg_driver_1_d), .c(dec_7seg_driver_1_c));  // open: dp
  _7_Segment_Display u_7_segment_display_2 (
    .g(dec_7seg_driver_2_g), .f(dec_7seg_driver_2_f), .a(dec_7seg_driver_2_a), .b(dec_7seg_driver_2_b),
    .e(dec_7seg_driver_2_e), .d(dec_7seg_driver_2_d), .c(dec_7seg_driver_2_c));  // open: dp
  dec_7seg_driver dec_7seg_driver_3 (
    .W(in_10), .X(in_6), .Y(tens_place_true_1_h), .Z(tens_place_true_1_i), .A(dec_7seg_driver_3_a),
    .B(dec_7seg_driver_3_b), .C(dec_7seg_driver_3_c), .D(dec_7seg_driver_3_d), .E(dec_7seg_driver_3_e),
    .F(dec_7seg_driver_3_f), .G(dec_7seg_driver_3_g));
  _7_Segment_Display u_7_segment_display_3 (
    .g(dec_7seg_driver_3_g), .f(dec_7seg_driver_3_f), .a(dec_7seg_driver_3_a), .b(dec_7seg_driver_3_b),
    .e(dec_7seg_driver_3_e), .d(dec_7seg_driver_3_d), .c(dec_7seg_driver_3_c));  // open: dp
  _7_Segment_Display u_7_segment_display_4 (
    .g(dec_7seg_driver_4_g), .f(dec_7seg_driver_4_f), .a(dec_7seg_driver_4_a), .b(dec_7seg_driver_4_b),
    .e(dec_7seg_driver_4_e), .d(dec_7seg_driver_4_d), .c(dec_7seg_driver_4_c));  // open: dp
  ones_place ones_place_1 (
    .A(dec_adder_1_out_9), .B(dec_adder_1_out_10), .C(dec_adder_1_out_11), .D(dec_adder_1_out_12),
    .E(dec_adder_1_out_13), .out_6(ones_place_1_out_6), .out_7(ones_place_1_out_7),
    .out_8(ones_place_1_out_8), .out_9(ones_place_1_out_9));
  dec_7seg_driver dec_7seg_driver_4 (
    .W(ones_place_1_out_6), .X(ones_place_1_out_7), .Y(ones_place_1_out_8), .Z(ones_place_1_out_9),
    .A(dec_7seg_driver_4_a), .B(dec_7seg_driver_4_b), .C(dec_7seg_driver_4_c), .D(dec_7seg_driver_4_d),
    .E(dec_7seg_driver_4_e), .F(dec_7seg_driver_4_f), .G(dec_7seg_driver_4_g));

  // Notes on the sheet:
  //   0
  //   0
  //   the columns are 4 bit integers
  //   2
  //   1
  //   8
  //   4
endmodule

module bonus (
  input  in_1,
  input  in_2,
  input  _1,
  input  _2,
  input  _3,
  input  in_6,
  input  in_7,
  input  in_8,
  input  in_9,
  input  in_10,
  input  in_11,
  input  in_12,
  input  in_13,
  input  in_14,
  input  in_15,
  input  in_16,
  input  in_17,
  input  in_18,
  input  in_19,
  input  in_20,
  input  in_21,
  input  in_22,
  input  _1_2,
  input  _2_2,
  input  _3_2,
  input  in_26,
  input  in_27,
  input  in_28,
  input  in_29,
  input  in_30,
  input  in_31,
  input  in_32,
  input  in_33,
  input  in_34,
  input  in_35,
  input  in_36,
  input  in_37,
  input  in_38
);

  wire dec_7seg_driver_1_a, dec_7seg_driver_1_b, dec_7seg_driver_1_c, dec_7seg_driver_1_d,
       dec_7seg_driver_1_e, dec_7seg_driver_1_f, dec_7seg_driver_1_g, dec_7seg_driver_2_a,
       dec_7seg_driver_2_b, dec_7seg_driver_2_c, dec_7seg_driver_2_d, dec_7seg_driver_2_e,
       dec_7seg_driver_2_f, dec_7seg_driver_2_g, dec_adder_1_out_9, dec_adder_1_out_10, dec_adder_1_out_11,
       dec_adder_1_out_12, dec_adder_1_out_13, hex_7seg_driver_1_a, hex_7seg_driver_1_b, hex_7seg_driver_1_c,
       hex_7seg_driver_1_d, hex_7seg_driver_1_e, hex_7seg_driver_1_f, hex_7seg_driver_1_g,
       hex_7seg_driver_2_a, hex_7seg_driver_2_b, hex_7seg_driver_2_c, hex_7seg_driver_2_d,
       hex_7seg_driver_2_e, hex_7seg_driver_2_f, hex_7seg_driver_2_g, n2_to_4_mux_set_1_out_0,
       n2_to_4_mux_set_1_out_1, n2_to_4_mux_set_1_out_2, n2_to_4_mux_set_1_out_3, n2_to_4_mux_set_2_out_0,
       n2_to_4_mux_set_2_out_1, n2_to_4_mux_set_2_out_2, n2_to_4_mux_set_2_out_3, ones_place_1_out_6,
       ones_place_1_out_7, ones_place_1_out_8, ones_place_1_out_9, tens_place_true_1_h, tens_place_true_1_i;

  _2_to_4_mux_set u_2_to_4_mux_set_1 (
    .a0(_1), .b0(_2), .c0(_3), .d0(in_7), .a1(in_8), .b1(in_9), .c1(in_11), .d1(in_12), .a2(in_13),
    .b2(in_14), .c2(in_15), .d2(in_16), .a3(in_17), .b3(in_18), .c3(in_19), .d3(in_20), .S1(in_1), .S0(in_2),
    .out_0(n2_to_4_mux_set_1_out_0), .out_1(n2_to_4_mux_set_1_out_1), .out_2(n2_to_4_mux_set_1_out_2),
    .out_3(n2_to_4_mux_set_1_out_3));
  _2_to_4_mux_set u_2_to_4_mux_set_2 (
    .a0(_1_2), .b0(_2_2), .c0(_3_2), .d0(in_26), .a1(in_27), .b1(in_28), .c1(in_29), .d1(in_30), .a2(in_31),
    .b2(in_32), .c2(in_33), .d2(in_34), .a3(in_35), .b3(in_36), .c3(in_37), .d3(in_38), .S1(in_21),
    .S0(in_22), .out_0(n2_to_4_mux_set_2_out_0), .out_1(n2_to_4_mux_set_2_out_1),
    .out_2(n2_to_4_mux_set_2_out_2), .out_3(n2_to_4_mux_set_2_out_3));
  tens_place_true tens_place_true_1 (
    .A(dec_adder_1_out_9), .B(dec_adder_1_out_10), .C(dec_adder_1_out_11), .D(dec_adder_1_out_12),
    .E(dec_adder_1_out_13), .H(tens_place_true_1_h), .I(tens_place_true_1_i));
  hex_7seg_driver hex_7seg_driver_1 (
    .W(n2_to_4_mux_set_1_out_3), .X(n2_to_4_mux_set_1_out_2), .Y(n2_to_4_mux_set_1_out_1),
    .Z(n2_to_4_mux_set_1_out_0), .A(hex_7seg_driver_1_a), .B(hex_7seg_driver_1_b), .C(hex_7seg_driver_1_c),
    .D(hex_7seg_driver_1_d), .E(hex_7seg_driver_1_e), .F(hex_7seg_driver_1_f), .G(hex_7seg_driver_1_g));
  hex_7seg_driver hex_7seg_driver_2 (
    .W(n2_to_4_mux_set_2_out_3), .X(n2_to_4_mux_set_2_out_2), .Y(n2_to_4_mux_set_2_out_1),
    .Z(n2_to_4_mux_set_2_out_0), .A(hex_7seg_driver_2_a), .B(hex_7seg_driver_2_b), .C(hex_7seg_driver_2_c),
    .D(hex_7seg_driver_2_d), .E(hex_7seg_driver_2_e), .F(hex_7seg_driver_2_f), .G(hex_7seg_driver_2_g));
  dec_adder dec_adder_1 (
    .in_1(n2_to_4_mux_set_1_out_3), .in_2(n2_to_4_mux_set_1_out_2), .in_3(n2_to_4_mux_set_1_out_1),
    .in_4(n2_to_4_mux_set_1_out_0), .in_5(n2_to_4_mux_set_2_out_3), .in_6(n2_to_4_mux_set_2_out_2),
    .in_7(n2_to_4_mux_set_2_out_1), .in_8(n2_to_4_mux_set_2_out_0), .out_9(dec_adder_1_out_9),
    .out_10(dec_adder_1_out_10), .out_11(dec_adder_1_out_11), .out_12(dec_adder_1_out_12),
    .out_13(dec_adder_1_out_13));
  _7_Segment_Display u_7_segment_display_1 (
    .g(hex_7seg_driver_1_g), .f(hex_7seg_driver_1_f), .a(hex_7seg_driver_1_a), .b(hex_7seg_driver_1_b),
    .e(hex_7seg_driver_1_e), .d(hex_7seg_driver_1_d), .c(hex_7seg_driver_1_c));  // open: dp
  _7_Segment_Display u_7_segment_display_2 (
    .g(hex_7seg_driver_2_g), .f(hex_7seg_driver_2_f), .a(hex_7seg_driver_2_a), .b(hex_7seg_driver_2_b),
    .e(hex_7seg_driver_2_e), .d(hex_7seg_driver_2_d), .c(hex_7seg_driver_2_c));  // open: dp
  dec_7seg_driver dec_7seg_driver_1 (
    .W(in_10), .X(in_6), .Y(tens_place_true_1_h), .Z(tens_place_true_1_i), .A(dec_7seg_driver_1_a),
    .B(dec_7seg_driver_1_b), .C(dec_7seg_driver_1_c), .D(dec_7seg_driver_1_d), .E(dec_7seg_driver_1_e),
    .F(dec_7seg_driver_1_f), .G(dec_7seg_driver_1_g));
  _7_Segment_Display u_7_segment_display_3 (
    .g(dec_7seg_driver_1_g), .f(dec_7seg_driver_1_f), .a(dec_7seg_driver_1_a), .b(dec_7seg_driver_1_b),
    .e(dec_7seg_driver_1_e), .d(dec_7seg_driver_1_d), .c(dec_7seg_driver_1_c));  // open: dp
  _7_Segment_Display u_7_segment_display_4 (
    .g(dec_7seg_driver_2_g), .f(dec_7seg_driver_2_f), .a(dec_7seg_driver_2_a), .b(dec_7seg_driver_2_b),
    .e(dec_7seg_driver_2_e), .d(dec_7seg_driver_2_d), .c(dec_7seg_driver_2_c));  // open: dp
  ones_place ones_place_1 (
    .A(dec_adder_1_out_9), .B(dec_adder_1_out_10), .C(dec_adder_1_out_11), .D(dec_adder_1_out_12),
    .E(dec_adder_1_out_13), .out_6(ones_place_1_out_6), .out_7(ones_place_1_out_7),
    .out_8(ones_place_1_out_8), .out_9(ones_place_1_out_9));
  dec_7seg_driver dec_7seg_driver_2 (
    .W(ones_place_1_out_6), .X(ones_place_1_out_7), .Y(ones_place_1_out_8), .Z(ones_place_1_out_9),
    .A(dec_7seg_driver_2_a), .B(dec_7seg_driver_2_b), .C(dec_7seg_driver_2_c), .D(dec_7seg_driver_2_d),
    .E(dec_7seg_driver_2_e), .F(dec_7seg_driver_2_f), .G(dec_7seg_driver_2_g));

  // Notes on the sheet:
  //   0
  //   0
  //   the columns are 4 bit integers
  //   2
  //   1
  //   8
  //   4
endmodule

module dec_7seg_driver (
  input  W,
  input  X,
  input  Y,
  input  Z,
  output A,
  output B,
  output C,
  output D,
  output E,
  output F,
  output G
);

  wire not_1_out, not_2_out, not_3_out, not_4_out, not_5_out, not_6_out, not_7_out, not_8_out, not_9_out,
       not_10_out, not_11_out, not_12_out, not_13_out, not_14_out, not_15_out, not_16_out, not_17_out,
       not_18_out, not_19_out, not_20_out, not_21_out, not_22_out, not_23_out, not_24_out, not_25_out,
       not_26_out, not_27_out, not_28_out, not_29_out, not_30_out, not_31_out, not_32_out, not_33_out,
       not_34_out, not_35_out, not_36_out, not_37_out, not_38_out, not_39_out, not_40_out, not_41_out,
       not_42_out, not_43_out, not_44_out, not_45_out, not_46_out, not_47_out, w_prime_x_2_out,
       w_prime_x_out, w_prime_x_prime_out, w_prime_x_prime_y_2_out, w_prime_x_prime_y_out,
       w_prime_xy_prime_out, w_prime_xy_prime_z_out, w_prime_xz_out, w_prime_y_out,
       w_prime_y_prime_z_prime_out, w_prime_yz_out, w_prime_yz_prime_2_out, w_prime_yz_prime_3_out,
       w_prime_yz_prime_out, w_prime_z_out, wx_prime_y_prime_2_out, wx_prime_y_prime_3_out,
       wx_prime_y_prime_out, x_prime_y_prime_2_out, x_prime_y_prime_out, x_prime_y_prime_z_prime_2_out,
       x_prime_y_prime_z_prime_3_out, x_prime_y_prime_z_prime_4_out, x_prime_y_prime_z_prime_out;

  not not_1 (not_1_out, Y);
  not not_2 (not_2_out, W);
  not not_3 (not_3_out, Y);
  not not_4 (not_4_out, X);
  not not_5 (not_5_out, X);
  not not_6 (not_6_out, W);
  not not_7 (not_7_out, Z);
  not not_8 (not_8_out, W);
  not not_9 (not_9_out, W);
  and w_prime_y (w_prime_y_out, Y, not_9_out);
  and w_prime_xz (w_prime_xz_out, Z, X, not_10_out);
  not not_10 (not_10_out, W);
  not not_11 (not_11_out, Y);
  not not_12 (not_12_out, X);
  and wx_prime_y_prime (wx_prime_y_prime_out, not_11_out, not_12_out, W);
  not not_13 (not_13_out, Z);
  not not_14 (not_14_out, Y);
  and x_prime_y_prime_z_prime (x_prime_y_prime_z_prime_out, not_13_out, not_14_out, not_15_out);
  not not_15 (not_15_out, X);
  not not_16 (not_16_out, X);
  and w_prime_x_prime (w_prime_x_prime_out, not_16_out, not_17_out);
  not not_17 (not_17_out, W);
  not not_18 (not_18_out, X);
  not not_19 (not_19_out, Y);
  and x_prime_y_prime (x_prime_y_prime_out, not_18_out, not_19_out);
  not not_20 (not_20_out, Z);
  and w_prime_y_prime_z_prime (w_prime_y_prime_z_prime_out, not_20_out, not_21_out, not_22_out);
  not not_21 (not_21_out, Y);
  not not_22 (not_22_out, W);
  and w_prime_yz (w_prime_yz_out, Z, Y, not_23_out);
  not not_23 (not_23_out, W);
  not not_24 (not_24_out, Y);
  not not_25 (not_25_out, X);
  and x_prime_y_prime_2 (x_prime_y_prime_2_out, not_24_out, not_25_out);
  not not_26 (not_26_out, W);
  and w_prime_x (w_prime_x_out, X, not_26_out);
  and w_prime_z (w_prime_z_out, Z, not_27_out);
  not not_27 (not_27_out, W);
  not not_28 (not_28_out, Y);
  and w_prime_xy_prime_z (w_prime_xy_prime_z_out, Z, not_28_out, X, not_29_out);
  not not_29 (not_29_out, W);
  not not_30 (not_30_out, Z);
  not not_31 (not_31_out, Y);
  and x_prime_y_prime_z_prime_2 (x_prime_y_prime_z_prime_2_out, not_30_out, not_31_out, not_32_out);
  not not_32 (not_32_out, X);
  not not_33 (not_33_out, X);
  and w_prime_x_prime_y (w_prime_x_prime_y_out, Y, not_33_out, not_34_out);
  not not_34 (not_34_out, W);
  not not_35 (not_35_out, Z);
  and w_prime_yz_prime (w_prime_yz_prime_out, not_35_out, Y, not_36_out);
  not not_36 (not_36_out, W);
  not not_37 (not_37_out, Z);
  not not_38 (not_38_out, Y);
  and x_prime_y_prime_z_prime_3 (x_prime_y_prime_z_prime_3_out, not_37_out, not_38_out, not_39_out);
  not not_39 (not_39_out, X);
  not not_40 (not_40_out, Z);
  and w_prime_yz_prime_2 (w_prime_yz_prime_2_out, not_40_out, Y, not_41_out);
  not not_41 (not_41_out, W);
  and w_prime_x_2 (w_prime_x_2_out, X, not_42_out);
  not not_42 (not_42_out, W);
  not not_43 (not_43_out, Z);
  not not_44 (not_44_out, Y);
  and x_prime_y_prime_z_prime_4 (x_prime_y_prime_z_prime_4_out, not_43_out, not_44_out, not_45_out);
  not not_45 (not_45_out, X);
  not not_46 (not_46_out, Y);
  not not_47 (not_47_out, X);
  and wx_prime_y_prime_2 (wx_prime_y_prime_2_out, not_46_out, not_47_out, W);
  and w_prime_xy_prime (w_prime_xy_prime_out, not_1_out, X, not_2_out);
  and wx_prime_y_prime_3 (wx_prime_y_prime_3_out, not_3_out, not_4_out, W);
  and w_prime_x_prime_y_2 (w_prime_x_prime_y_2_out, Y, not_5_out, not_6_out);
  and w_prime_yz_prime_3 (w_prime_yz_prime_3_out, not_7_out, Y, not_8_out);
  or or_1 (A, w_prime_y_out, w_prime_xz_out, wx_prime_y_prime_out, x_prime_y_prime_z_prime_out);
  or or_2 (B, w_prime_x_prime_out, x_prime_y_prime_out, w_prime_y_prime_z_prime_out, w_prime_yz_out);
  or or_3 (C, x_prime_y_prime_2_out, w_prime_x_out, w_prime_z_out);
  or or_4 (D, w_prime_xy_prime_z_out, x_prime_y_prime_z_prime_2_out, w_prime_x_prime_y_out, w_prime_yz_prime_out);
  or or_5 (E, x_prime_y_prime_z_prime_3_out, w_prime_yz_prime_2_out);
  or or_6 (F, w_prime_x_2_out, x_prime_y_prime_z_prime_4_out, wx_prime_y_prime_2_out);
  or or_7 (G, w_prime_xy_prime_out, wx_prime_y_prime_3_out, w_prime_x_prime_y_2_out, w_prime_yz_prime_3_out);
endmodule

module dec_counter (
  input  Clock,
  output _0,
  output _1,
  output _2,
  output _3,
  output IS_NINE
);

  wire and_2_out, and_3_out, and_4_out, and_5_out, and_6_out, and_7_out, and_8_out, D1_qn, D2_qn, D3_qn,
       D4_qn, or_1_out, or_2_out, or_3_out;

  and and_1 (IS_NINE, _3, D2_qn, D3_qn, _0);
  and and_2 (and_2_out, _3, D4_qn);
  and and_3 (and_3_out, _2, _1, _0);
  and and_4 (and_4_out, _2, D3_qn);
  and and_5 (and_5_out, _2, D4_qn);
  and and_6 (and_6_out, D2_qn, _1, _0);
  and and_7 (and_7_out, _1, D4_qn);
  and and_8 (and_8_out, D1_qn, D3_qn, _0);
  or or_1 (or_1_out, and_2_out, and_3_out);
  or or_2 (or_2_out, and_4_out, and_5_out, and_6_out);
  or or_3 (or_3_out, and_7_out, and_8_out);
  D_Flip_Flop #(.trigger("falling")) D1 (.clk(Clock), .D(or_1_out), .Q(_3), .Qn(D1_qn));  // open: preset, en, reset
  D_Flip_Flop #(.trigger("falling")) D2 (.clk(Clock), .D(or_2_out), .Q(_2), .Qn(D2_qn));  // open: preset, en, reset
  D_Flip_Flop #(.trigger("falling")) D3 (.clk(Clock), .D(or_3_out), .Q(_1), .Qn(D3_qn));  // open: preset, en, reset
  D_Flip_Flop #(.trigger("falling")) D4 (.clk(Clock), .D(D4_qn), .Q(_0), .Qn(D4_qn));  // open: preset, en, reset
endmodule

module hex_7seg_driver (
  input  W,
  input  X,
  input  Y,
  input  Z,
  output A,
  output B,
  output C,
  output D,
  output E,
  output F,
  output G
);

  wire and_1_out, and_2_out, and_3_out, and_4_out, and_5_out, and_6_out, and_7_out, and_8_out, and_9_out,
       and_10_out, and_11_out, and_12_out, and_13_out, and_14_out, and_15_out, and_16_out, and_17_out,
       and_18_out, and_19_out, and_20_out, and_21_out, and_22_out, and_23_out, and_24_out, and_25_out,
       and_26_out, and_27_out, and_28_out, and_29_out, and_30_out, and_31_out, and_32_out, and_33_out,
       and_34_out, and_35_out, and_36_out;

  and and_1 (and_1_out, ~X, ~Z);  // AND_Gate
  and and_2 (and_2_out, ~W, Y);  // AND_Gate
  and and_3 (and_3_out, X, Y);
  and and_4 (and_4_out, W, ~Z);  // AND_Gate
  and and_5 (and_5_out, ~W, X, Z);  // AND_Gate
  and and_6 (and_6_out, W, ~X, ~Y);  // AND_Gate
  and and_7 (and_7_out, ~W, ~X);  // AND_Gate
  and and_8 (and_8_out, ~X, ~Z);  // AND_Gate
  and and_9 (and_9_out, ~W, ~Y, ~Z);  // AND_Gate
  and and_10 (and_10_out, ~W, Y, Z);  // AND_Gate
  and and_11 (and_11_out, W, ~Y, Z);  // AND_Gate
  and and_12 (and_12_out, ~W, ~Y);  // AND_Gate
  and and_13 (and_13_out, ~W, Z);  // AND_Gate
  and and_14 (and_14_out, ~Y, Z);  // AND_Gate
  and and_15 (and_15_out, ~W, X);  // AND_Gate
  and and_16 (and_16_out, W, ~X);  // AND_Gate
  and and_17 (and_17_out, ~W, ~X, Y);  // AND_Gate
  and and_18 (and_18_out, ~W, ~X, ~Z);  // AND_Gate
  and and_19 (and_19_out, X, Y, ~Z);  // AND_Gate
  and and_20 (and_20_out, W, ~X, Z);  // AND_Gate
  and and_21 (and_21_out, W, ~Y);  // AND_Gate
  and and_22 (and_22_out, X, ~Y, Z);  // AND_Gate
  and and_23 (and_23_out, ~X, ~Z);  // AND_Gate
  and and_24 (and_24_out, W, X);
  and and_25 (and_25_out, W, Y);
  and and_26 (and_26_out, Y, ~Z);  // AND_Gate
  and and_27 (and_27_out, X, ~Z);  // AND_Gate
  and and_28 (and_28_out, W, ~X);  // AND_Gate
  and and_29 (and_29_out, W, Y);
  and and_30 (and_30_out, ~W, ~Y, ~Z);  // AND_Gate
  and and_31 (and_31_out, ~W, ~Y, X);  // AND_Gate
  and and_32 (and_32_out, ~X, Y);  // AND_Gate
  and and_33 (and_33_out, Y, ~Z);  // AND_Gate
  and and_34 (and_34_out, W, ~X);  // AND_Gate
  and and_35 (and_35_out, W, Z);
  and and_36 (and_36_out, ~W, X, ~Y);  // AND_Gate
  or or_1 (A, and_1_out, and_2_out, and_3_out, and_4_out, and_5_out, and_6_out);
  or or_2 (B, and_7_out, and_8_out, and_9_out, and_10_out, and_11_out);
  or or_3 (C, and_12_out, and_13_out, and_14_out, and_15_out, and_16_out);
  or or_4 (D, and_17_out, and_18_out, and_19_out, and_20_out, and_21_out, and_22_out);
  or or_5 (E, and_23_out, and_24_out, and_25_out, and_26_out);
  or or_6 (F, and_27_out, and_28_out, and_29_out, and_30_out, and_31_out);
  or or_7 (G, and_32_out, and_33_out, and_34_out, and_35_out, and_36_out);
endmodule

module hex_counter (
  input  Clock,
  output _0,
  output _1,
  output _2,
  output _3,
  output IS_FIFTEEN
);

  wire and_2_out, and_3_out, and_4_out, and_5_out, and_6_out, and_7_out, and_8_out, and_9_out, and_10_out,
       D1_qn, D2_qn, D3_qn, D4_qn, or_1_out, or_2_out, or_3_out;

  and and_1 (IS_FIFTEEN, _3, _2, _1, _0);
  and and_2 (and_2_out, _3, D2_qn);
  and and_3 (and_3_out, _3, D3_qn);
  and and_4 (and_4_out, _3, D4_qn);
  and and_5 (and_5_out, D1_qn, _2, _1, _0);
  and and_6 (and_6_out, _2, D3_qn);
  and and_7 (and_7_out, _2, D4_qn);
  and and_8 (and_8_out, D2_qn, _1, _0);
  and and_9 (and_9_out, _1, D4_qn);
  and and_10 (and_10_out, D3_qn, _0);
  or or_1 (or_1_out, and_2_out, and_3_out, and_4_out, and_5_out);
  or or_2 (or_2_out, and_6_out, and_7_out, and_8_out);
  or or_3 (or_3_out, and_9_out, and_10_out);
  D_Flip_Flop #(.trigger("falling")) D1 (.clk(Clock), .D(or_1_out), .Q(_3), .Qn(D1_qn));  // open: preset, en, reset
  D_Flip_Flop #(.trigger("falling")) D2 (.clk(Clock), .D(or_2_out), .Q(_2), .Qn(D2_qn));  // open: preset, en, reset
  D_Flip_Flop #(.trigger("falling")) D3 (.clk(Clock), .D(or_3_out), .Q(_1), .Qn(D3_qn));  // open: preset, en, reset
  D_Flip_Flop #(.trigger("falling")) D4 (.clk(Clock), .D(D4_qn), .Q(_0), .Qn(D4_qn));  // open: preset, en, reset
endmodule

module dec_adder (
  input  in_1,
  input  in_2,
  input  in_3,
  input  in_4,
  input  in_5,
  input  in_6,
  input  in_7,
  input  in_8,
  output out_9,
  output out_10,
  output out_11,
  output out_12,
  output out_13
);

  wire dec_3bit_adder_1_out_4, dec_3bit_adder_3_out_4, dec__2bit_adder_1_out_4;

  dec__2bit_adder dec__2bit_adder_1 (.in_1(in_4), .in_2(in_8), .out_3(out_13), .out_4(dec__2bit_adder_1_out_4));
  dec_3bit_adder dec_3bit_adder_1 (
    .out_5(out_12), .out_4(dec_3bit_adder_1_out_4), .in_1(dec__2bit_adder_1_out_4), .in_2(in_3), .in_3(in_7));
  dec_3bit_adder dec_3bit_adder_2 (
    .out_5(out_10), .out_4(out_9), .in_1(dec_3bit_adder_3_out_4), .in_2(in_1), .in_3(in_5));
  dec_3bit_adder dec_3bit_adder_3 (
    .out_5(out_11), .out_4(dec_3bit_adder_3_out_4), .in_1(dec_3bit_adder_1_out_4), .in_2(in_2), .in_3(in_6));
endmodule

module dec__2bit_adder (
  input  in_1,
  input  in_2,
  output out_3,
  output out_4
);

  wire and_2_out, nor_1_out;

  and and_1 (out_4, in_2, in_1);
  nor nor_1 (nor_1_out, in_1, in_2);
  and and_2 (and_2_out, in_1, in_2);
  nor nor_2 (out_3, nor_1_out, and_2_out);
endmodule

module dec_3bit_adder (
  input  in_1,
  input  in_2,
  input  in_3,
  output out_4,
  output out_5
);

  wire and_1_out, and_2_out, and_3_out, and_4_out, and_5_out, and_6_out, and_7_out;

  and and_1 (and_1_out, in_1, ~in_2, ~in_3);  // AND_Gate
  and and_2 (and_2_out, ~in_1, ~in_2, in_3);  // AND_Gate
  and and_3 (and_3_out, in_1, in_2, in_3);
  and and_4 (and_4_out, ~in_1, in_2, ~in_3);  // AND_Gate
  and and_5 (and_5_out, in_2, in_3);
  and and_6 (and_6_out, in_1, in_3);
  and and_7 (and_7_out, in_1, in_2);
  or or_1 (out_5, and_1_out, and_2_out, and_3_out, and_4_out);
  or or_2 (out_4, and_5_out, and_6_out, and_7_out);
endmodule

module ones_place (
  input  A,
  input  B,
  input  C,
  input  D,
  input  E,
  output out_6,
  output out_7,
  output out_8,
  output out_9
);

  wire and_1_out, and_2_out, and_3_out, and_4_out, and_5_out, and_6_out, and_7_out, and_8_out, and_9_out,
       and_10_out, and_11_out, and_12_out;

  and and_1 (and_1_out, ~A, B, ~C, ~D);  // AND_Gate
  and and_2 (and_2_out, A, B, C, ~D);  // AND_Gate
  and and_3 (and_3_out, A, ~B, ~C, D);  // AND_Gate
  and and_4 (and_4_out, ~A, ~B, C);  // AND_Gate
  and and_5 (and_5_out, ~A, C, D);  // AND_Gate
  and and_6 (and_6_out, A, B, ~C);  // AND_Gate
  and and_7 (and_7_out, A, ~B, ~C, ~D);  // AND_Gate
  and and_8 (and_8_out, ~A, ~B, D);  // AND_Gate
  and and_9 (and_9_out, ~A, B, C, ~D);  // AND_Gate
  and and_10 (and_10_out, A, B, ~C, D);  // AND_Gate
  and and_11 (and_11_out, A, ~B, C, D);  // AND_Gate
  and and_12 (and_12_out, A, ~B, ~C, ~D);  // AND_Gate
  or or_1 (out_6, and_1_out, and_2_out, and_3_out);
  or or_2 (out_7, and_4_out, and_5_out, and_6_out, and_7_out);
  or or_3 (out_8, and_8_out, and_9_out, and_10_out, and_11_out, and_12_out);

  assign out_9 = E;
endmodule

module tens_place_true (
  input  A,
  input  B,
  input  C,
  input  D,
  input  E,
  output H,
  output I
);

  wire and_1_out, and_2_out, and_3_out, and_4_out, and_5_out, and_7_out, not_1_out, not_2_out, not_3_out,
       or_1_out, or_2_out, or_3_out;

  not not_1 (not_1_out, A);
  and and_1 (and_1_out, B, C);
  and and_2 (and_2_out, D, B);
  or or_1 (or_1_out, B, C);
  not not_2 (not_2_out, B);
  and and_3 (and_3_out, not_2_out, not_3_out);
  not not_3 (not_3_out, C);
  or or_2 (or_2_out, and_1_out, and_2_out);
  and and_4 (and_4_out, D, C, B);
  and and_5 (and_5_out, not_1_out, or_2_out);
  and and_6 (H, A, or_1_out);
  or or_3 (or_3_out, and_3_out, and_4_out);
  and and_7 (and_7_out, A, or_3_out);
  or or_4 (I, and_5_out, and_7_out);
endmodule

module _4_way_mux (
  input  S_1,
  input  S_0,
  input  W,
  input  X,
  input  Y,
  input  Z,
  output out_7
);

  wire and_1_out, and_2_out, and_3_out, and_4_out, not_1_out, not_2_out;

  not not_1 (not_1_out, S_1);
  not not_2 (not_2_out, S_0);
  and and_1 (and_1_out, not_2_out, W, not_1_out);
  and and_2 (and_2_out, S_0, X, not_1_out);
  and and_3 (and_3_out, not_2_out, Y, S_1);
  and and_4 (and_4_out, S_0, Z, S_1);
  or or_1 (out_7, and_1_out, and_2_out, and_3_out, and_4_out);
endmodule

module _2_to_4_mux_set (
  input  S1,
  input  S0,
  input  a0,
  input  b0,
  input  c0,
  input  d0,
  input  a1,
  input  b1,
  input  c1,
  input  d1,
  input  a2,
  input  b2,
  input  c2,
  input  d2,
  input  a3,
  input  b3,
  input  c3,
  input  d3,
  output out_0,
  output out_1,
  output out_2,
  output out_3
);

  _4_way_mux u_4_way_mux_1 (.W(a0), .X(b0), .Y(c0), .Z(d0), .S_1(S1), .S_0(S0), .out_7(out_0));
  _4_way_mux u_4_way_mux_2 (.W(a1), .X(b1), .Y(c1), .Z(d1), .S_1(S1), .S_0(S0), .out_7(out_1));
  _4_way_mux u_4_way_mux_3 (.W(a2), .X(b2), .Y(c2), .Z(d2), .S_1(S1), .S_0(S0), .out_7(out_2));
  _4_way_mux u_4_way_mux_4 (.W(a3), .X(b3), .Y(c3), .Z(d3), .S_1(S1), .S_0(S0), .out_7(out_3));
endmodule
