// Logisim project Project3.circ as structural Verilog: 3 circuits, main circuit main
module main (
  input  in_1
);

  wire clock_1_out, n1to6counter_1_a, n1to6counter_1_b, n1to6counter_1_c, n1to6counter_1_out_3,
       n7segmentdriver_1_a, n7segmentdriver_1_b, n7segmentdriver_1_c, n7segmentdriver_1_d,
       n7segmentdriver_1_e, n7segmentdriver_1_f, n7segmentdriver_1_g, n7segmentdriver_2_a,
       n7segmentdriver_2_b, n7segmentdriver_2_c, n7segmentdriver_2_d, n7segmentdriver_2_e,
       n7segmentdriver_2_f, n7segmentdriver_2_g, undriven, undriven_2, undriven_3, undriven_4;

  Clock clock_1 (.out(clock_1_out));
  _1To6Counter u_1to6counter_1 (
    .A(n1to6counter_1_a), .B(n1to6counter_1_b), .C(n1to6counter_1_c), .x(in_1), .clock(clock_1_out),
    .out_3(n1to6counter_1_out_3));  // open: Reset
  _7SegmentDriver u_7segmentdriver_1 (
    .W(n1to6counter_1_out_3), .X(n1to6counter_1_a), .Y(n1to6counter_1_b), .Z(n1to6counter_1_c),
    .A(n7segmentdriver_1_a), .B(n7segmentdriver_1_b), .C(n7segmentdriver_1_c), .D(n7segmentdriver_1_d),
    .E(n7segmentdriver_1_e), .F(n7segmentdriver_1_f), .G(n7segmentdriver_1_g));
  _7SegmentDriver u_7segmentdriver_2 (
    .W(undriven), .X(undriven_2), .Y(undriven_3), .Z(undriven_4), .A(n7segmentdriver_2_a),
    .B(n7segmentdriver_2_b), .C(n7segmentdriver_2_c), .D(n7segmentdriver_2_d), .E(n7segmentdriver_2_e),
    .F(n7segmentdriver_2_f), .G(n7segmentdriver_2_g));
  _7_Segment_Display u_7_segment_display_1 (
    .g(n7segmentdriver_1_g), .f(n7segmentdriver_1_f), .a(n7segmentdriver_1_a), .b(n7segmentdriver_1_b),
    .e(n7segmentdriver_1_e), .d(n7segmentdriver_1_d), .c(n7segmentdriver_1_c));  // open: dp
  _7_Segment_Display u_7_segment_display_2 (
    .g(n7segmentdriver_2_g), .f(n7segmentdriver_2_f), .a(n7segmentdriver_2_a), .b(n7segmentdriver_2_b),
    .e(n7segmentdriver_2_e), .d(n7segmentdriver_2_d), .c(n7segmentdriver_2_c));  // open: dp
endmodule

module _1To6Counter (
  input  clock,
  input  x,
  output out_3,
  output A,
  output B,
  output C,
  output Reset
);

  wire A_qn, and_1_out, and_2_out, and_3_out, and_4_out, and_5_out, and_6_out, and_7_out, and_8_out, B_qn,
       C_qn, not_1_out, or_1_out, or_2_out;

  not not_1 (not_1_out, x);
  and and_1 (and_1_out, x, A, C);
  and and_2 (and_2_out, not_1_out, B, C);
  and and_3 (and_3_out, not_1_out, A, C_qn);
  and and_4 (and_4_out, x, A_qn, B_qn, C_qn);
  and and_5 (and_5_out, x, B, C);
  and and_6 (and_6_out, x, A, C_qn);
  and and_7 (and_7_out, not_1_out, B, C_qn);
  and and_8 (and_8_out, not_1_out, A_qn, B_qn, C);
  or or_1 (or_1_out, and_1_out, and_2_out, and_3_out, and_4_out);
  or or_2 (or_2_out, and_5_out, and_6_out, and_7_out, and_8_out);
  D_Flip_Flop u_A (.clk(clock), .D(or_1_out), .Q(A), .Qn(A_qn));  // open: preset, en, reset
  D_Flip_Flop u_B (.clk(clock), .D(or_2_out), .Q(B), .Qn(B_qn));  // open: preset, en, reset
  D_Flip_Flop u_C (.clk(clock), .D(C_qn), .Q(C), .Qn(C_qn));  // open: preset, en, reset
  and and_9 (Reset, A_qn, B_qn, C_qn);

  assign out_3 = 1'b0;
endmodule

module _7SegmentDriver (
  input  W,
  input  X,
  input  Y,
  input  Z,
  output A,
  output B,
  output C,
  output D,
  output E,
  output F,
  output G
);

  wire not_1_out, not_2_out, not_3_out, not_4_out, not_5_out, not_6_out, not_7_out, not_8_out, not_9_out,
       not_10_out, not_11_out, not_12_out, not_13_out, not_14_out, not_15_out, not_16_out, not_17_out,
       not_18_out, not_19_out, not_20_out, not_21_out, not_22_out, not_23_out, not_24_out, not_25_out,
       not_26_out, not_27_out, not_28_out, not_29_out, not_30_out, not_31_out, not_32_out, not_33_out,
       not_34_out, not_35_out, not_36_out, not_37_out, not_38_out, not_39_out, not_40_out, not_41_out,
       not_42_out, not_43_out, not_44_out, not_45_out, not_46_out, not_47_out, w_prime_x_2_out,
       w_prime_x_out, w_prime_x_prime_out, w_prime_x_prime_y_2_out, w_prime_x_prime_y_out,
       w_prime_xy_prime_out, w_prime_xy_prime_z_out, w_prime_xz_out, w_prime_y_out,
       w_prime_y_prime_z_prime_out, w_prime_yz_out, w_prime_yz_prime_2_out, w_prime_yz_prime_3_out,
       w_prime_yz_prime_out, w_prime_z_out, wx_prime_y_prime_2_out, wx_prime_y_prime_3_out,
       wx_prime_y_prime_out, x_prime_y_prime_2_out, x_prime_y_prime_out, x_prime_y_prime_z_prime_2_out,
       x_prime_y_prime_z_prime_3_out, x_prime_y_prime_z_prime_4_out, x_prime_y_prime_z_prime_out;

  not not_1 (not_1_out, W);
  not not_2 (not_2_out, W);
  not not_3 (not_3_out, Y);
  not not_4 (not_4_out, X);
  not not_5 (not_5_out, Z);
  not not_6 (not_6_out, Y);
  not not_7 (not_7_out, X);
  not not_8 (not_8_out, X);
  not not_9 (not_9_out, W);
  not not_10 (not_10_out, X);
  not not_11 (not_11_out, Y);
  not not_12 (not_12_out, Z);
  not not_13 (not_13_out, Y);
  not not_14 (not_14_out, W);
  not not_15 (not_15_out, W);
  not not_16 (not_16_out, Y);
  not not_17 (not_17_out, X);
  not not_18 (not_18_out, W);
  not not_19 (not_19_out, W);
  not not_20 (not_20_out, Y);
  not not_21 (not_21_out, W);
  not not_22 (not_22_out, Z);
  not not_23 (not_23_out, Y);
  not not_24 (not_24_out, X);
  not not_25 (not_25_out, X);
  not not_26 (not_26_out, W);
  not not_27 (not_27_out, Z);
  not not_28 (not_28_out, W);
  not not_29 (not_29_out, Z);
  not not_30 (not_30_out, Y);
  not not_31 (not_31_out, X);
  not not_32 (not_32_out, Z);
  not not_33 (not_33_out, W);
  not not_34 (not_34_out, W);
  not not_35 (not_35_out, Z);
  not not_36 (not_36_out, Y);
  not not_37 (not_37_out, X);
  not not_38 (not_38_out, Y);
  not not_39 (not_39_out, X);
  not not_40 (not_40_out, Y);
  not not_41 (not_41_out, W);
  not not_42 (not_42_out, Y);
  not not_43 (not_43_out, X);
  not not_44 (not_44_out, X);
  not not_45 (not_45_out, W);
  not not_46 (not_46_out, Z);
  not not_47 (not_47_out, W);
  and w_prime_y (w_prime_y_out, Y, not_1_out);
  and w_prime_xz (w_prime_xz_out, Z, X, not_2_out);
  and wx_prime_y_prime (wx_prime_y_prime_out, not_3_out, not_4_out, W);
  and x_prime_y_prime_z_prime (x_prime_y_prime_z_prime_out, not_5_out, not_6_out, not_7_out);
  and w_prime_x_prime (w_prime_x_prime_out, not_8_out, not_9_out);
  and x_prime_y_prime (x_prime_y_prime_out, not_10_out, not_11_out);
  and w_prime_y_prime_z_prime (w_prime_y_prime_z_prime_out, not_12_out, not_13_out, not_14_out);
  and w_prime_yz (w_prime_yz_out, Z, Y, not_15_out);
  and x_prime_y_prime_2 (x_prime_y_prime_2_out, not_16_out, not_17_out);
  and w_prime_x (w_prime_x_out, X, not_18_out);
  and w_prime_z (w_prime_z_out, Z, not_19_out);
  and w_prime_xy_prime_z (w_prime_xy_prime_z_out, Z, not_20_out, X, not_21_out);
  and x_prime_y_prime_z_prime_2 (x_prime_y_prime_z_prime_2_out, not_22_out, not_23_out, not_24_out);
  and w_prime_x_prime_y (w_prime_x_prime_y_out, Y, not_25_out, not_26_out);
  and w_prime_yz_prime (w_prime_yz_prime_out, not_27_out, Y, not_28_out);
  and x_prime_y_prime_z_prime_3 (x_prime_y_prime_z_prime_3_out, not_29_out, not_30_out, not_31_out);
  and w_prime_yz_prime_2 (w_prime_yz_prime_2_out, not_32_out, Y, not_33_out);
  and w_prime_x_2 (w_prime_x_2_out, X, not_34_out);
  and x_prime_y_prime_z_prime_4 (x_prime_y_prime_z_prime_4_out, not_35_out, not_36_out, not_37_out);
  and wx_prime_y_prime_2 (wx_prime_y_prime_2_out, not_38_out, not_39_out, W);
  and w_prime_xy_prime (w_prime_xy_prime_out, not_40_out, X, not_41_out);
  and wx_prime_y_prime_3 (wx_prime_y_prime_3_out, not_42_out, not_43_out, W);
  and w_prime_x_prime_y_2 (w_prime_x_prime_y_2_out, Y, not_44_out, not_45_out);
  and w_prime_yz_prime_3 (w_prime_yz_prime_3_out, not_46_out, Y, not_47_out);
  or or_1 (A, w_prime_y_out, w_prime_xz_out, wx_prime_y_prime_out, x_prime_y_prime_z_prime_out);
  or or_2 (B, w_prime_x_prime_out, x_prime_y_prime_out, w_prime_y_prime_z_prime_out, w_prime_yz_out);
  or or_3 (C, x_prime_y_prime_2_out, w_prime_x_out, w_prime_z_out);
  or or_4 (D, w_prime_xy_prime_z_out, x_prime_y_prime_z_prime_2_out, w_prime_x_prime_y_out, w_prime_yz_prime_out);
  or or_5 (E, x_prime_y_prime_z_prime_3_out, w_prime_yz_prime_2_out);
  or or_6 (F, w_prime_x_2_out, x_prime_y_prime_z_prime_4_out, wx_prime_y_prime_2_out);
  or or_7 (G, w_prime_xy_prime_out, wx_prime_y_prime_3_out, w_prime_x_prime_y_2_out, w_prime_yz_prime_3_out);
endmodule
