// Logisim project Project3_122429am.circ as structural Verilog: 4 circuits, main circuit main
module main (
  input  in_1
);

  wire clock_1_out, n1to6counter_1_a, n1to6counter_1_b, n1to6counter_1_c, n1to6counter_1_out_3,
       n4bit_counter_1_a, n4bit_counter_1_b, n4bit_counter_1_c, n4bit_counter_1_d, n4bit_counter_1_reset,
       n7segmentdriver_1_a, n7segmentdriver_1_b, n7segmentdriver_1_c, n7segmentdriver_1_d,
       n7segmentdriver_1_e, n7segmentdriver_1_f, n7segmentdriver_1_g, n7segmentdriver_2_a,
       n7segmentdriver_2_b, n7segmentdriver_2_c, n7segmentdriver_2_d, n7segmentdriver_2_e,
       n7segmentdriver_2_f, n7segmentdriver_2_g;

  _1To6Counter u_1to6counter_1 (
    .A(n1to6counter_1_a), .B(n1to6counter_1_b), .C(n1to6counter_1_c), .x(in_1),
    .clock(n4bit_counter_1_reset), .out_3(n1to6counter_1_out_3));
  _4bit_counter u_4bit_counter_1 (
    .A(n4bit_counter_1_a), .B(n4bit_counter_1_b), .D(n4bit_counter_1_d), .C(n4bit_counter_1_c), .x(in_1),
    .Clock(clock_1_out), .reset(n4bit_counter_1_reset));
  Clock clock_1 (.out(clock_1_out));
  _7SegmentDriver u_7segmentdriver_1 (
    .W(n1to6counter_1_out_3), .X(n1to6counter_1_a), .Y(n1to6counter_1_b), .Z(n1to6counter_1_c),
    .A(n7segmentdriver_1_a), .B(n7segmentdriver_1_b), .C(n7segmentdriver_1_c), .D(n7segmentdriver_1_d),
    .E(n7segmentdriver_1_e), .F(n7segmentdriver_1_f), .G(n7segmentdriver_1_g));
  _7SegmentDriver u_7segmentdriver_2 (
    .W(n4bit_counter_1_d), .X(n4bit_counter_1_c), .Y(n4bit_counter_1_b), .Z(n4bit_counter_1_a),
    .A(n7segmentdriver_2_a), .B(n7segmentdriver_2_b), .C(n7segmentdriver_2_c), .D(n7segmentdriver_2_d),
    .E(n7segmentdriver_2_e), .F(n7segmentdriver_2_f), .G(n7segmentdriver_2_g));
  _7_Segment_Display u_7_segment_display_1 (
    .g(n7segmentdriver_1_g), .f(n7segmentdriver_1_f), .a(n7segmentdriver_1_a), .b(n7segmentdriver_1_b),
    .e(n7segmentdriver_1_e), .d(n7segmentdriver_1_d), .c(n7segmentdriver_1_c));  // open: dp
  _7_Segment_Display u_7_segment_display_2 (
    .g(n7segmentdriver_2_g), .f(n7segmentdriver_2_f), .a(n7segmentdriver_2_a), .b(n7segmentdriver_2_b),
    .e(n7segmentdriver_2_e), .d(n7segmentdriver_2_d), .c(n7segmentdriver_2_c));  // open: dp
endmodule

module _1To6Counter (
  input  clock,
  input  x,
  output out_3,
  output A,
  output B,
  output C
);

  wire A_qn, and_1_out, and_2_out, and_3_out, and_4_out, and_5_out, and_6_out, and_7_out, and_8_out, B_qn,
       C_qn, not_1_out, or_1_out, or_2_out;

  not not_1 (not_1_out, x);
  and and_1 (and_1_out, x, A, C);
  and and_2 (and_2_out, not_1_out, B, C);
  and and_3 (and_3_out, not_1_out, A, C_qn);
  and and_4 (and_4_out, x, A_qn, B_qn, C_qn);
  and and_5 (and_5_out, x, B, C);
  and and_6 (and_6_out, x, A, C_qn);
  and and_7 (and_7_out, not_1_out, B, C_qn);
  and and_8 (and_8_out, not_1_out, A_qn, B_qn, C);
  or or_1 (or_1_out, and_1_out, and_2_out, and_3_out, and_4_out);
  or or_2 (or_2_out, and_5_out, and_6_out, and_7_out, and_8_out);
  D_Flip_Flop u_A (.clk(clock), .D(or_1_out), .Q(A), .Qn(A_qn));  // open: preset, en, reset
  D_Flip_Flop u_B (.clk(clock), .D(or_2_out), .Q(B), .Qn(B_qn));  // open: preset, en, reset
  D_Flip_Flop u_C (.clk(clock), .D(C_qn), .Q(C), .Qn(C_qn));  // open: preset, en, reset

  assign out_3 = 1'b0;
endmodule

module _7SegmentDriver (
  input  W,
  input  X,
  input  Y,
  input  Z,
  output A,
  output B,
  output C,
  output D,
  output E,
  output F,
  output G
);

  wire not_1_out, not_2_out, not_3_out, not_4_out, not_5_out, not_6_out, not_7_out, not_8_out, not_9_out,
       not_10_out, not_11_out, not_12_out, not_13_out, not_14_out, not_15_out, not_16_out, not_17_out,
       not_18_out, not_19_out, not_20_out, not_21_out, not_22_out, not_23_out, not_24_out, not_25_out,
       not_26_out, not_27_out, not_28_out, not_29_out, not_30_out, not_31_out, not_32_out, not_33_out,
       not_34_out, not_35_out, not_36_out, not_37_out, not_38_out, not_39_out, not_40_out, not_41_out,
       not_42_out, not_43_out, not_44_out, not_45_out, not_46_out, not_47_out, w_prime_x_2_out,
       w_prime_x_out, w_prime_x_prime_out, w_prime_x_prime_y_2_out, w_prime_x_prime_y_out,
       w_prime_xy_prime_out, w_prime_xy_prime_z_out, w_prime_xz_out, w_prime_y_out,
       w_prime_y_prime_z_prime_out, w_prime_yz_out, w_prime_yz_prime_2_out, w_prime_yz_prime_3_out,
       w_prime_yz_prime_out, w_prime_z_out, wx_prime_y_prime_2_out, wx_prime_y_prime_3_out,
       wx_prime_y_prime_out, x_prime_y_prime_2_out, x_prime_y_prime_out, x_prime_y_prime_z_prime_2_out,
       x_prime_y_prime_z_prime_3_out, x_prime_y_prime_z_prime_4_out, x_prime_y_prime_z_prime_out;

  not not_1 (not_1_out, W);
  not not_2 (not_2_out, W);
  not not_3 (not_3_out, Y);
  not not_4 (not_4_out, X);
  not not_5 (not_5_out, Z);
  not not_6 (not_6_out, Y);
  not not_7 (not_7_out, X);
  not not_8 (not_8_out, X);
  not not_9 (not_9_out, W);
  not not_10 (not_10_out, X);
  not not_11 (not_11_out, Y);
  not not_12 (not_12_out, Z);
  not not_13 (not_13_out, Y);
  not not_14 (not_14_out, W);
  not not_15 (not_15_out, W);
  not not_16 (not_16_out, Y);
  not not_17 (not_17_out, X);
  not not_18 (not_18_out, W);
  not not_19 (not_19_out, W);
  not not_20 (not_20_out, Y);
  not not_21 (not_21_out, W);
  not not_22 (not_22_out, Z);
  not not_23 (not_23_out, Y);
  not not_24 (not_24_out, X);
  not not_25 (not_25_out, X);
  not not_26 (not_26_out, W);
  not not_27 (not_27_out, Z);
  not not_28 (not_28_out, W);
  not not_29 (not_29_out, Z);
  not not_30 (not_30_out, Y);
  not not_31 (not_31_out, X);
  not not_32 (not_32_out, Z);
  not not_33 (not_33_out, W);
  not not_34 (not_34_out, W);
  not not_35 (not_35_out, Z);
  not not_36 (not_36_out, Y);
  not not_37 (not_37_out, X);
  not not_38 (not_38_out, Y);
  not not_39 (not_39_out, X);
  not not_40 (not_40_out, Y);
  not not_41 (not_41_out, W);
  not not_42 (not_42_out, Y);
  not not_43 (not_43_out, X);
  not not_44 (not_44_out, X);
  not not_45 (not_45_out, W);
  not not_46 (not_46_out, Z);
  not not_47 (not_47_out, W);
  and w_prime_y (w_prime_y_out, Y, not_1_out);
  and w_prime_xz (w_prime_xz_out, Z, X, not_2_out);
  and wx_prime_y_prime (wx_prime_y_prime_out, not_3_out, not_4_out, W);
  and x_prime_y_prime_z_prime (x_prime_y_prime_z_prime_out, not_5_out, not_6_out, not_7_out);
  and w_prime_x_prime (w_prime_x_prime_out, not_8_out, not_9_out);
  and x_prime_y_prime (x_prime_y_prime_out, not_10_out, not_11_out);
  and w_prime_y_prime_z_prime (w_prime_y_prime_z_prime_out, not_12_out, not_13_out, not_14_out);
  and w_prime_yz (w_prime_yz_out, Z, Y, not_15_out);
  and x_prime_y_prime_2 (x_prime_y_prime_2_out, not_16_out, not_17_out);
  and w_prime_x (w_prime_x_out, X, not_18_out);
  and w_prime_z (w_prime_z_out, Z, not_19_out);
  and w_prime_xy_prime_z (w_prime_xy_prime_z_out, Z, not_20_out, X, not_21_out);
  and x_prime_y_prime_z_prime_2 (x_prime_y_prime_z_prime_2_out, not_22_out, not_23_out, not_24_out);
  and w_prime_x_prime_y (w_prime_x_prime_y_out, Y, not_25_out, not_26_out);
  and w_prime_yz_prime (w_prime_yz_prime_out, not_27_out, Y, not_28_out);
  and x_prime_y_prime_z_prime_3 (x_prime_y_prime_z_prime_3_out, not_29_out, not_30_out, not_31_out);
  and w_prime_yz_prime_2 (w_prime_yz_prime_2_out, not_32_out, Y, not_33_out);
  and w_prime_x_2 (w_prime_x_2_out, X, not_34_out);
  and x_prime_y_prime_z_prime_4 (x_prime_y_prime_z_prime_4_out, not_35_out, not_36_out, not_37_out);
  and wx_prime_y_prime_2 (wx_prime_y_prime_2_out, not_38_out, not_39_out, W);
  and w_prime_xy_prime (w_prime_xy_prime_out, not_40_out, X, not_41_out);
  and wx_prime_y_prime_3 (wx_prime_y_prime_3_out, not_42_out, not_43_out, W);
  and w_prime_x_prime_y_2 (w_prime_x_prime_y_2_out, Y, not_44_out, not_45_out);
  and w_prime_yz_prime_3 (w_prime_yz_prime_3_out, not_46_out, Y, not_47_out);
  or or_1 (A, w_prime_y_out, w_prime_xz_out, wx_prime_y_prime_out, x_prime_y_prime_z_prime_out);
  or or_2 (B, w_prime_x_prime_out, x_prime_y_prime_out, w_prime_y_prime_z_prime_out, w_prime_yz_out);
  or or_3 (C, x_prime_y_prime_2_out, w_prime_x_out, w_prime_z_out);
  or or_4 (D, w_prime_xy_prime_z_out, x_prime_y_prime_z_prime_2_out, w_prime_x_prime_y_out, w_prime_yz_prime_out);
  or or_5 (E, x_prime_y_prime_z_prime_3_out, w_prime_yz_prime_2_out);
  or or_6 (F, w_prime_x_2_out, x_prime_y_prime_z_prime_4_out, wx_prime_y_prime_2_out);
  or or_7 (G, w_prime_xy_prime_out, wx_prime_y_prime_3_out, w_prime_x_prime_y_2_out, w_prime_yz_prime_3_out);
endmodule

module _4bit_counter (
  input  x,
  input  Clock,
  output A,
  output B,
  output D,
  output C,
  output reset
);

  wire A_qn, and_1_out, and_2_out, and_3_out, and_4_out, and_5_out, and_6_out, and_7_out, and_8_out,
       and_9_out, and_10_out, and_11_out, and_12_out, and_13_out, and_14_out, and_15_out, and_16_out,
       and_17_out, B_qn, C_qn, D_qn, Ka_is_perpetually_true_out, not_1_out, not_2_out, not_3_out, or_1_out,
       or_2_out, or_3_out, or_4_out, or_5_out, or_6_out, or_7_out, or_8_out, or_9_out, or_11_out;

  and and_1 (and_1_out, A_qn, B_qn, C_qn, x);
  not not_1 (not_1_out, x);
  and and_2 (and_2_out, B_qn, A_qn, x);
  and and_3 (and_3_out, and_2_out, D);
  or or_1 (or_1_out, and_2_out, and_6_out);
  and and_4 (and_4_out, not_1_out, C, B, A);
  or or_2 (or_2_out, and_4_out, and_1_out);
  and and_5 (and_5_out, B_qn, A_qn, x);
  and and_6 (and_6_out, not_1_out, B, A);
  or or_3 (or_3_out, and_3_out, and_6_out);
  and and_7 (and_7_out, not_1_out, B);
  or or_4 (or_4_out, and_7_out, and_5_out);
  J_K_Flip_Flop u_C (
    .J(or_3_out), .clk(Clock), .K(or_1_out), .Q(C), .Qn(C_qn), .reset(and_13_out));  // open: preset, en
  J_K_Flip_Flop u_D (
    .J(or_2_out), .clk(Clock), .K(or_4_out), .Q(D), .Qn(D_qn), .reset(and_13_out));  // open: preset, en
  and and_8 (and_8_out, C, B_qn);
  and and_9 (and_9_out, x, A_qn);
  or or_5 (or_5_out, and_8_out, D);
  and and_10 (and_10_out, x, or_5_out, A_qn);
  or or_6 (or_6_out, D, A);
  and and_11 (and_11_out, not_1_out, or_6_out);
  or or_7 (or_7_out, and_9_out, and_11_out);
  and and_12 (and_12_out, not_1_out, A);
  or or_8 (or_8_out, and_10_out, and_12_out);
  J_K_Flip_Flop u_B (
    .J(or_8_out), .clk(Clock), .K(or_7_out), .Q(B), .Qn(B_qn), .reset(and_13_out));  // open: preset, en
  and and_13 (and_13_out, D, not_2_out, B, not_3_out, not_1_out);
  not not_2 (not_2_out, C);
  not not_3 (not_3_out, A);
  buf and_14 (and_14_out, x);  // AND_Gate
  or Ka_is_perpetually_true (Ka_is_perpetually_true_out, x, not_1_out);
  and and_15 (and_15_out, ~D, ~C, ~x, ~B, ~A);  // AND_Gate
  and and_16 (and_16_out, not_1_out, or_11_out);
  or or_9 (or_9_out, and_14_out, and_16_out);
  and and_17 (and_17_out, D, ~C, x, ~B, A);  // AND_Gate
  or or_10 (reset, and_15_out, and_17_out);
  or or_11 (or_11_out, B_qn, D_qn);
  J_K_Flip_Flop u_A (
    .J(or_9_out), .clk(Clock), .K(Ka_is_perpetually_true_out), .Q(A), .Qn(A_qn), .reset(and_13_out));  // open: preset, en
endmodule
